# Fritzing sketch sketch (saved by Fritzing 0.9.3b)
breadboards: 1

parts:
  U1 = NodeMCU V3.0
  VCC1 = Battery block 9V
  J3 = Basic Servo
  VCC2 = 4 x AAA Battery Mount  # not connected

nets:
  N1: U1.D0, U1.RST
  3V3: U1.3V3, J3.vcc
  N2: U1.GND#6, U1.GND#13, U1.GND#16, U1.GND#33, VCC1.-, J3.gnd
  N3: U1.D6, J3.pulse
  N4: U1.Vin, VCC1.+

notes:
  5-10V to power ESP8266
  3-5V to power Servo
  9 V or
  4 x 1.5 V

custom parts:
  NodeMCU V3.0: ESP8266 based NodeMCU
